# Fritzing sketch WakeOnTime (saved by Fritzing 0.9.3b)
breadboards: 1

parts:
  Part2 = Arduino Nano (Rev3.0)
  IRF9520 = Basic FET P-Channel [package="TO220 [THT]"]
  R1 = Resistor [tolerance=±5% resistance=10k package="2010 [SMD]"]
  Part1 = Adafruit DS3231 [part_number="Adafruit #3013"]
  Voltage_regulator_5V = Voltage Regulator [package=to-92]
  Minimum_6_5V = Battery block 9V
  R2 = Resistor [tolerance=±5% resistance=100 package="2010 [SMD]"]

nets:
  GND: Part2.GND, Part1.GND, Voltage_regulator_5V.GND, Minimum_6_5V.-, R2.Pin_1
  N1: Part2.VIN, IRF9520.drain, R2.Pin_0
  N2: Part2.A5, Part1.SCL
  N3: Part2.A4, Part1.SDA
  N4: IRF9520.gate, R1.Pin_1, Part1.SQW
  N5: IRF9520.source, Voltage_regulator_5V.IN, Minimum_6_5V.+
  N6: R1.Pin_0, Part1.Vin, Voltage_regulator_5V.OUT

custom parts:
  Adafruit DS3231: The datasheet for the DS3231 explains that this part is an "Extremely Accurate I²C-Integrated RTC/TCXO/Crystal". And, hey, it does exactly what it says on the tin! This Real Time Clock (RTC) is the most precise you can get in a small, low power package. Most RTCs use an external 32kHz timing crystal that is used to keep time with low current draw. And that's all well and good, but those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
